// Logisim project 8_bit_arithmetic_unit.circ as structural Verilog: 9 circuits, main circuit main
module main (
);

  wire A0, A1, A2, A3, A4, A5, A6, A7, B0, B1, B2, B3, B4, B5, B6, B7, E, G, L, N, n_t;
  wire [3:0] D0, D1, D2, input_display_1_out_2, input_display_1_out_3, input_display_1_out_4,
       input_display_2_out_2, input_display_2_out_3, input_display_2_out_4, S0, S1, S2;

  // DipSwitch dipswitch_1: pin names not known
  LED led_1 (.in(A7));
  // DipSwitch dipswitch_2: pin names not known
  LED led_2 (.in(B7));
  Adder_circ adder_circ_1 (
    .a7(A7), .a6(A6), .a5(A5), .a4(A4), .a3(A3), .a2(A2), .a1(A1), .a0(A0), .b7(B7), .b6(B6), .b5(B5),
    .b4(B4), .b3(B3), .b2(B2), .b1(B1), .b0(B0), .s2(S2), .s1(S1), .s0(S0), .N(N));
  Hex_Digit_Display hex_digit_display_1 (.value(input_display_1_out_2));  // open: dp
  Hex_Digit_Display hex_digit_display_2 (.value(input_display_1_out_3));  // open: dp
  Hex_Digit_Display hex_digit_display_3 (.value(input_display_2_out_2));  // open: dp
  Hex_Digit_Display hex_digit_display_4 (.value(input_display_1_out_4));  // open: dp
  Hex_Digit_Display hex_digit_display_5 (.value(input_display_2_out_3));  // open: dp
  Hex_Digit_Display hex_digit_display_6 (.value(input_display_2_out_4));  // open: dp
  Input_Display input_display_1 (
    .I({A7, A6, A5, A4, A3, A2, A1, A0}), .out_2(input_display_1_out_2), .out_3(input_display_1_out_3),
    .out_4(input_display_1_out_4));
  Input_Display input_display_2 (
    .I({B7, B6, B5, B4, B3, B2, B1, B0}), .out_2(input_display_2_out_2), .out_3(input_display_2_out_3),
    .out_4(input_display_2_out_4));
  Subtractor_circ subtractor_circ_1 (
    .a7(A7), .a6(A6), .a5(A5), .a4(A4), .a3(A3), .a2(A2), .a1(A1), .a0(A0), .b7(B7), .b6(B6), .b5(B5),
    .b4(B4), .b3(B3), .b2(B2), .b1(B1), .b0(B0), .D2(D2), .D1(D1), .D0(D0), .N(n_t));
  LED led_3 (.in(N));
  LED led_4 (.in(n_t));
  Hex_Digit_Display hex_digit_display_7 (.value(S2));  // open: dp
  Hex_Digit_Display hex_digit_display_8 (.value(D2));  // open: dp
  Hex_Digit_Display hex_digit_display_9 (.value(S1));  // open: dp
  Hex_Digit_Display hex_digit_display_10 (.value(S0));  // open: dp
  Hex_Digit_Display hex_digit_display_11 (.value(D1));  // open: dp
  Hex_Digit_Display hex_digit_display_12 (.value(D0));  // open: dp
  LED led_5 (.in(G));
  LED led_6 (.in(E));
  LED led_7 (.in(L));
  Comparator_circ comparator_circ_1 (
    .a7(A7), .a6(A6), .a5(A5), .a4(A4), .a3(A3), .a2(A2), .a1(A1), .a0(A0), .b7(B7), .b6(B6), .b5(B5),
    .b4(B4), .b3(B3), .b2(B2), .b1(B1), .b0(B0), .E(E), .G(G), .L(L));

  // Notes on the sheet:
  //   NEG
  //   NEG
  //   A + B
  //   A - B
  //   A > B
  //   A = B
  //   A < B
endmodule

module Full_Adder (
  input  A,
  input  B,
  input  Cin,
  output Cout,
  output S
);

  wire and_1_out, and_2_out, and_3_out, xor_1_out;

  xor xor_1 (xor_1_out, A, B);
  and and_1 (and_1_out, A, B);
  and and_2 (and_2_out, A, Cin);
  and and_3 (and_3_out, B, Cin);
  or or_1 (Cout, and_1_out, and_2_out, and_3_out);
  xor xor_2 (S, xor_1_out, Cin);
endmodule

module Ripple_Carry_Adder (
  input  A7,
  input  B7,
  input  A6,
  input  B6,
  input  A5,
  input  B5,
  input  A4,
  input  B4,
  input  A3,
  input  B3,
  input  A2,
  input  B2,
  input  A1,
  input  B1,
  input  A0,
  input  B0,
  output V,
  output S7,
  output S6,
  output S5,
  output S4,
  output S3,
  output S2,
  output S1,
  output S0
);

  wire full_adder_1_cout, full_adder_2_cout, full_adder_3_cout, full_adder_4_cout, full_adder_5_cout,
       full_adder_6_cout, full_adder_7_cout, full_adder_8_cout;

  Full_Adder full_adder_1 (.A(A7), .B(B7), .Cin(full_adder_2_cout), .Cout(full_adder_1_cout), .S(S7));
  Full_Adder full_adder_2 (.A(A6), .B(B6), .Cin(full_adder_3_cout), .Cout(full_adder_2_cout), .S(S6));
  Full_Adder full_adder_3 (.A(A5), .B(B5), .Cin(full_adder_4_cout), .Cout(full_adder_3_cout), .S(S5));
  Full_Adder full_adder_4 (.A(A4), .B(B4), .Cin(full_adder_5_cout), .Cout(full_adder_4_cout), .S(S4));
  Full_Adder full_adder_5 (.A(A3), .B(B3), .Cin(full_adder_6_cout), .Cout(full_adder_5_cout), .S(S3));
  Full_Adder full_adder_6 (.A(A2), .B(B2), .Cin(full_adder_7_cout), .Cout(full_adder_6_cout), .S(S2));
  Full_Adder full_adder_7 (.A(A1), .B(B1), .Cin(full_adder_8_cout), .Cout(full_adder_7_cout), .S(S1));
  Full_Adder full_adder_8 (.A(A0), .B(B0), .Cout(full_adder_8_cout), .S(S0));  // open: Cin
  xor xor_1 (V, full_adder_1_cout, full_adder_2_cout);
endmodule

module Input_Display (
  input  [7:0] I,
  output [3:0] out_2,
  output [3:0] out_3,
  output [3:0] out_4
);

  wire [7:0] divider_1_out, divider_2_out, two_s_complement_1_out_17;
  wire [7:4] divider_1_rem, divider_2_rem, divider_3_rem;

  Two_s_Complement two_s_complement_1 (
    .in_1(I[7]), .in_2(I[7]), .in_3(I[6]), .in_4(I[5]), .in_5(I[4]), .in_6(I[3]), .in_7(I[2]), .in_8(I[1]),
    .in_9(I[0]), .out_10(two_s_complement_1_out_17[7]), .out_11(two_s_complement_1_out_17[6]),
    .out_12(two_s_complement_1_out_17[5]), .out_13(two_s_complement_1_out_17[4]),
    .out_14(two_s_complement_1_out_17[3]), .out_15(two_s_complement_1_out_17[2]),
    .out_16(two_s_complement_1_out_17[1]), .out_17(two_s_complement_1_out_17[0]));
  Divider divider_1 (
    .a(two_s_complement_1_out_17), .b(8'ha), .out(divider_1_out), .upper({8{1'b0}}),
    .rem({divider_1_rem, out_4}));
  Divider divider_2 (.a(divider_1_out), .b(8'ha), .out(divider_2_out), .upper({8{1'b0}}), .rem({divider_2_rem, out_3}));
  Divider divider_3 (.a(divider_2_out), .b(8'ha), .rem({divider_3_rem, out_2}));  // open: out, upper
endmodule

module Comparator_circ (
  input  a7,
  input  a6,
  input  a5,
  input  a4,
  input  a3,
  input  a2,
  input  a1,
  input  a0,
  input  b7,
  input  b6,
  input  b5,
  input  b4,
  input  b3,
  input  b2,
  input  b1,
  input  b0,
  output E,
  output G,
  output L
);

  wire A0_t, A1_t, A2_t, A3_t, A4_t, A5_t, A6_t, A7_t, and_1_out, and_2_out, and_3_out, and_4_out, and_5_out,
       and_6_out, and_7_out, and_8_out, and_9_out, and_10_out, and_11_out, and_12_out, and_13_out,
       and_14_out, and_15_out, and_16_out, and_17_out, and_18_out, and_19_out, and_20_out, and_21_out,
       and_22_out, and_23_out, and_24_out, and_25_out, and_26_out, and_27_out, and_28_out, and_29_out,
       and_30_out, and_31_out, and_32_out, and_33_out, and_34_out, and_35_out, and_37_out, and_38_out,
       and_39_out, and_40_out, B0_t, B1_t, B2_t, B3_t, B4_t, B5_t, B6_t, B7_t, not_1_out, not_2_out,
       not_3_out, not_4_out, not_5_out, not_6_out, not_7_out, not_8_out, not_9_out, not_10_out, not_11_out,
       not_12_out, not_13_out, not_14_out, not_15_out, not_16_out, not_17_out, not_18_out, or_1_out,
       or_2_out, xnor_1_out, xnor_2_out, xnor_3_out, xnor_4_out, xnor_5_out, xnor_6_out, xnor_7_out,
       xnor_8_out, xnor_9_out;

  Two_s_Complement two_s_complement_1 (
    .in_1(a7), .in_2(a7), .in_3(a6), .in_4(a5), .in_5(a4), .in_6(a3), .in_7(a2), .in_8(a1), .in_9(a0),
    .out_10(A7_t), .out_11(A6_t), .out_12(A5_t), .out_13(A4_t), .out_14(A3_t), .out_15(A2_t), .out_16(A1_t),
    .out_17(A0_t));
  Two_s_Complement two_s_complement_2 (
    .in_1(b7), .in_2(b7), .in_3(b6), .in_4(b5), .in_5(b4), .in_6(b3), .in_7(b2), .in_8(b1), .in_9(b0),
    .out_10(B7_t), .out_11(B6_t), .out_12(B5_t), .out_13(B4_t), .out_14(B3_t), .out_15(B2_t), .out_16(B1_t),
    .out_17(B0_t));
  xnor xnor_1 (xnor_1_out, A7_t, B7_t);
  xnor xnor_2 (xnor_2_out, A6_t, B6_t);
  xnor xnor_3 (xnor_3_out, A5_t, B5_t);
  xnor xnor_4 (xnor_4_out, A4_t, B4_t);
  xnor xnor_5 (xnor_5_out, A3_t, B3_t);
  xnor xnor_6 (xnor_6_out, A2_t, B2_t);
  xnor xnor_7 (xnor_7_out, A1_t, B1_t);
  xnor xnor_8 (xnor_8_out, A0_t, B0_t);
  and and_1 (and_1_out, A7_t, not_1_out);
  not not_1 (not_1_out, B7_t);
  and and_2 (and_2_out, A6_t, not_2_out);
  not not_2 (not_2_out, B6_t);
  and and_3 (and_3_out, A5_t, not_3_out);
  not not_3 (not_3_out, B5_t);
  and and_4 (and_4_out, A4_t, not_4_out);
  not not_4 (not_4_out, B4_t);
  and and_5 (and_5_out, A3_t, not_5_out);
  not not_5 (not_5_out, B3_t);
  and and_6 (and_6_out, A2_t, not_6_out);
  not not_6 (not_6_out, B2_t);
  and and_7 (and_7_out, A1_t, not_7_out);
  not not_7 (not_7_out, B1_t);
  and and_8 (and_8_out, A0_t, not_8_out);
  not not_8 (not_8_out, B0_t);
  not not_9 (not_9_out, A7_t);
  and and_9 (and_9_out, not_9_out, B7_t);
  not not_10 (not_10_out, A6_t);
  and and_10 (and_10_out, not_10_out, B6_t);
  not not_11 (not_11_out, A5_t);
  and and_11 (and_11_out, not_11_out, B5_t);
  not not_12 (not_12_out, A4_t);
  and and_12 (and_12_out, not_12_out, B4_t);
  not not_13 (not_13_out, A3_t);
  and and_13 (and_13_out, not_13_out, B3_t);
  not not_14 (not_14_out, A2_t);
  and and_14 (and_14_out, not_14_out, B2_t);
  not not_15 (not_15_out, A1_t);
  and and_15 (and_15_out, not_15_out, B1_t);
  not not_16 (not_16_out, A0_t);
  and and_16 (and_16_out, not_16_out, B0_t);
  and and_17 (and_17_out, xnor_1_out, and_2_out);
  and and_18 (and_18_out, xnor_1_out, xnor_2_out, and_3_out);
  and and_19 (and_19_out, xnor_1_out, xnor_2_out, xnor_3_out, and_4_out);
  and and_20 (and_20_out, xnor_1_out, xnor_2_out, xnor_3_out, xnor_4_out, and_5_out);
  and and_21 (and_21_out, xnor_1_out, xnor_2_out, xnor_3_out, xnor_4_out, and_6_out, xnor_5_out);
  and and_22 (and_22_out, xnor_1_out, xnor_2_out, xnor_3_out, xnor_6_out, xnor_4_out, and_7_out, xnor_5_out);
  and and_23 (and_23_out, xnor_1_out, xnor_2_out, xnor_3_out, xnor_4_out, and_8_out, xnor_5_out, xnor_6_out, xnor_7_out);
  and and_24 (and_24_out, xnor_1_out, and_10_out);
  and and_25 (and_25_out, xnor_1_out, xnor_2_out, and_11_out);
  and and_26 (and_26_out, xnor_1_out, xnor_2_out, xnor_3_out, and_12_out);
  and and_27 (and_27_out, xnor_1_out, xnor_2_out, xnor_3_out, xnor_4_out, and_13_out);
  and and_28 (and_28_out, xnor_1_out, xnor_2_out, xnor_3_out, xnor_4_out, and_14_out, xnor_5_out);
  and and_29 (and_29_out, xnor_1_out, xnor_2_out, xnor_3_out, xnor_4_out, xnor_5_out, and_15_out, xnor_6_out);
  and and_30 (and_30_out, xnor_1_out, xnor_2_out, xnor_3_out, xnor_4_out, and_16_out, xnor_5_out, xnor_6_out, xnor_7_out);
  and and_31 (and_31_out, xnor_1_out, xnor_2_out, xnor_3_out, xnor_4_out, xnor_5_out, xnor_6_out, xnor_7_out, xnor_8_out);
  or or_1 (or_1_out, and_1_out, and_17_out, and_18_out, and_19_out, and_20_out, and_21_out, and_22_out, and_23_out);
  or or_2 (or_2_out, and_9_out, and_24_out, and_25_out, and_26_out, and_27_out, and_28_out, and_29_out, and_30_out);
  not not_17 (not_17_out, b7);
  not not_18 (not_18_out, a7);
  and and_32 (and_32_out, b7, not_18_out);
  and and_33 (and_33_out, not_17_out, a7);
  and and_34 (and_34_out, not_18_out, not_17_out);
  and and_35 (and_35_out, a7, b7);
  xnor xnor_9 (xnor_9_out, b7, a7);
  and and_36 (E, xnor_9_out, and_31_out);
  and and_37 (and_37_out, or_1_out, and_34_out);
  and and_38 (and_38_out, or_2_out, and_35_out);
  and and_39 (and_39_out, or_2_out, and_34_out);
  and and_40 (and_40_out, or_1_out, and_35_out);
  or or_3 (G, and_37_out, and_32_out, and_38_out);
  or or_4 (L, and_39_out, and_33_out, and_40_out);
endmodule

module Adder_circ (
  input  a7,
  input  a6,
  input  a5,
  input  a4,
  input  a3,
  input  a2,
  input  a1,
  input  a0,
  input  b7,
  input  b6,
  input  b5,
  input  b4,
  input  b3,
  input  b2,
  input  b1,
  input  b0,
  output [3:0] s2,
  output [3:0] s1,
  output [3:0] s0,
  output N
);

  wire a0_t, a1_t, a2_t, a3_t, a4_t, a5_t, a6_t, a7_t, and_1_out, and_2_out, b0_t, b1_t, b2_t, b3_t, b4_t,
       b5_t, b6_t, b7_t, nand_1_out, not_1_out, not_2_out, ripple_carry_adder_1_s0, ripple_carry_adder_1_s1,
       ripple_carry_adder_1_s2, ripple_carry_adder_1_s3, ripple_carry_adder_1_s4, ripple_carry_adder_1_s5,
       ripple_carry_adder_1_s6, ripple_carry_adder_1_s7, ripple_carry_adder_1_v;

  and and_1 (and_1_out, a7, b7);
  Two_s_Complement two_s_complement_1 (
    .in_1(and_1_out), .in_2(a7), .in_3(a6), .in_4(a5), .in_5(a4), .in_6(a3), .in_7(a2), .in_8(a1), .in_9(a0),
    .out_10(a7_t), .out_11(a6_t), .out_12(a5_t), .out_13(a4_t), .out_14(a3_t), .out_15(a2_t), .out_16(a1_t),
    .out_17(a0_t));
  Two_s_Complement two_s_complement_2 (
    .in_1(and_1_out), .in_2(b7), .in_3(b6), .in_4(b5), .in_5(b4), .in_6(b3), .in_7(b2), .in_8(b1), .in_9(b0),
    .out_10(b7_t), .out_11(b6_t), .out_12(b5_t), .out_13(b4_t), .out_14(b3_t), .out_15(b2_t), .out_16(b1_t),
    .out_17(b0_t));
  Ripple_Carry_Adder ripple_carry_adder_1 (
    .A7(a7_t), .B7(b7_t), .A6(a6_t), .B6(b6_t), .A5(a5_t), .B5(b5_t), .A4(a4_t), .B4(b4_t), .A3(a3_t),
    .B3(b3_t), .A2(a2_t), .B2(b2_t), .A1(a1_t), .B1(b1_t), .A0(a0_t), .B0(b0_t), .V(ripple_carry_adder_1_v),
    .S7(ripple_carry_adder_1_s7), .S6(ripple_carry_adder_1_s6), .S5(ripple_carry_adder_1_s5),
    .S4(ripple_carry_adder_1_s4), .S3(ripple_carry_adder_1_s3), .S2(ripple_carry_adder_1_s2),
    .S1(ripple_carry_adder_1_s1), .S0(ripple_carry_adder_1_s0));
  nand nand_1 (nand_1_out, a7, b7);
  not not_1 (not_1_out, ripple_carry_adder_1_v);
  and and_2 (and_2_out, nand_1_out, not_1_out, ripple_carry_adder_1_s7);
  not not_2 (not_2_out, nand_1_out);
  or or_1 (N, and_2_out, not_2_out);
  Output_Display output_display_1 (
    .V(and_2_out), .R7(ripple_carry_adder_1_s7), .R6(ripple_carry_adder_1_s6), .R5(ripple_carry_adder_1_s5),
    .R4(ripple_carry_adder_1_s4), .R3(ripple_carry_adder_1_s3), .R2(ripple_carry_adder_1_s2),
    .R1(ripple_carry_adder_1_s1), .R0(ripple_carry_adder_1_s0), .out_10(s2), .out_11(s1), .out_12(s0));
endmodule

module Output_Display (
  input  V,
  input  R7,
  input  R6,
  input  R5,
  input  R4,
  input  R3,
  input  R2,
  input  R1,
  input  R0,
  output [3:0] out_10,
  output [3:0] out_11,
  output [3:0] out_12
);

  wire [7:0] divider_1_out, divider_2_out, two_s_complement_1_out_17;
  wire [7:4] divider_1_rem, divider_2_rem, divider_3_rem;

  Two_s_Complement two_s_complement_1 (
    .in_1(V), .in_2(R7), .in_3(R6), .in_4(R5), .in_5(R4), .in_6(R3), .in_7(R2), .in_8(R1), .in_9(R0),
    .out_10(two_s_complement_1_out_17[7]), .out_11(two_s_complement_1_out_17[6]),
    .out_12(two_s_complement_1_out_17[5]), .out_13(two_s_complement_1_out_17[4]),
    .out_14(two_s_complement_1_out_17[3]), .out_15(two_s_complement_1_out_17[2]),
    .out_16(two_s_complement_1_out_17[1]), .out_17(two_s_complement_1_out_17[0]));
  Divider divider_1 (
    .a(two_s_complement_1_out_17), .b(8'ha), .out(divider_1_out), .upper({8{1'b0}}),
    .rem({divider_1_rem, out_12}));
  Divider divider_2 (
    .a(divider_1_out), .b(8'ha), .out(divider_2_out), .upper({8{1'b0}}), .rem({divider_2_rem, out_11}));
  Divider divider_3 (.a(divider_2_out), .b(8'ha), .rem({divider_3_rem, out_10}));  // open: out, upper
endmodule

module Subtractor_circ (
  input  a7,
  input  a6,
  input  a5,
  input  a4,
  input  a3,
  input  a2,
  input  a1,
  input  a0,
  input  b7,
  input  b6,
  input  b5,
  input  b4,
  input  b3,
  input  b2,
  input  b1,
  input  b0,
  output [3:0] D2,
  output [3:0] D1,
  output [3:0] D0,
  output N
);

  wire and_1_out, and_2_out, and_3_out, and_4_out, nand_1_out, not_1_out, not_2_out, not_3_out, or_1_out,
       or_2_out, ripple_carry_adder_1_s0, ripple_carry_adder_1_s1, ripple_carry_adder_1_s2,
       ripple_carry_adder_1_s3, ripple_carry_adder_1_s4, ripple_carry_adder_1_s5, ripple_carry_adder_1_s6,
       ripple_carry_adder_1_s7, ripple_carry_adder_1_v, X0, X1, X2, X3, X4, X5, X6, X7, Y0, Y1, Y2, Y3, Y4,
       Y5, Y6, Y7;

  Two_s_Complement two_s_complement_1 (
    .in_1(1'b0), .in_2(a7), .in_3(a6), .in_4(a5), .in_5(a4), .in_6(a3), .in_7(a2), .in_8(a1), .in_9(a0),
    .out_10(X7), .out_11(X6), .out_12(X5), .out_13(X4), .out_14(X3), .out_15(X2), .out_16(X1), .out_17(X0));
  Two_s_Complement two_s_complement_2 (
    .in_1(1'b1), .in_2(b7), .in_3(b6), .in_4(b5), .in_5(b4), .in_6(b3), .in_7(b2), .in_8(b1), .in_9(b0),
    .out_10(Y7), .out_11(Y6), .out_12(Y5), .out_13(Y4), .out_14(Y3), .out_15(Y2), .out_16(Y1), .out_17(Y0));
  not not_1 (not_1_out, a7);
  not not_2 (not_2_out, b7);
  or or_1 (or_1_out, not_1_out, b7);
  not not_3 (not_3_out, ripple_carry_adder_1_v);
  Ripple_Carry_Adder ripple_carry_adder_1 (
    .A7(X7), .B7(Y7), .A6(X6), .B6(Y6), .A5(X5), .B5(Y5), .A4(X4), .B4(Y4), .A3(X3), .B3(Y3), .A2(X2),
    .B2(Y2), .A1(X1), .B1(Y1), .A0(X0), .B0(Y0), .V(ripple_carry_adder_1_v), .S7(ripple_carry_adder_1_s7),
    .S6(ripple_carry_adder_1_s6), .S5(ripple_carry_adder_1_s5), .S4(ripple_carry_adder_1_s4),
    .S3(ripple_carry_adder_1_s3), .S2(ripple_carry_adder_1_s2), .S1(ripple_carry_adder_1_s1),
    .S0(ripple_carry_adder_1_s0));
  nand nand_1 (nand_1_out, b7, Y7);
  and and_1 (and_1_out, a7, not_2_out);
  and and_2 (and_2_out, or_1_out, not_3_out, ripple_carry_adder_1_s7);
  or or_2 (or_2_out, and_1_out, and_2_out);
  and and_3 (and_3_out, not_2_out, a7);
  and and_4 (and_4_out, nand_1_out, or_2_out);
  or or_3 (N, and_4_out, and_3_out);
  Output_Display output_display_1 (
    .V(and_4_out), .R7(ripple_carry_adder_1_s7), .R6(ripple_carry_adder_1_s6), .R5(ripple_carry_adder_1_s5),
    .R4(ripple_carry_adder_1_s4), .R3(ripple_carry_adder_1_s3), .R2(ripple_carry_adder_1_s2),
    .R1(ripple_carry_adder_1_s1), .R0(ripple_carry_adder_1_s0), .out_10(D2), .out_11(D1), .out_12(D0));
endmodule

module Two_s_Complement (
  input  in_1,
  input  in_2,
  input  in_3,
  input  in_4,
  input  in_5,
  input  in_6,
  input  in_7,
  input  in_8,
  input  in_9,
  output out_10,
  output out_11,
  output out_12,
  output out_13,
  output out_14,
  output out_15,
  output out_16,
  output out_17
);

  wire full_adder_2_cout, full_adder_3_cout, full_adder_4_cout, full_adder_5_cout, full_adder_6_cout,
       full_adder_7_cout, full_adder_8_cout, xor_1_out, xor_2_out, xor_3_out, xor_4_out, xor_5_out,
       xor_6_out, xor_7_out, xor_8_out;

  xor xor_1 (xor_1_out, in_2, in_1);
  xor xor_2 (xor_2_out, in_3, in_1);
  xor xor_3 (xor_3_out, in_4, in_1);
  xor xor_4 (xor_4_out, in_5, in_1);
  xor xor_5 (xor_5_out, in_1, in_6);
  xor xor_6 (xor_6_out, in_1, in_7);
  xor xor_7 (xor_7_out, in_1, in_8);
  xor xor_8 (xor_8_out, in_1, in_9);
  Full_Adder full_adder_1 (.A(xor_1_out), .B(1'b0), .Cin(full_adder_2_cout), .S(out_10));  // open: Cout
  Full_Adder full_adder_2 (.A(xor_2_out), .B(1'b0), .Cin(full_adder_3_cout), .Cout(full_adder_2_cout), .S(out_11));
  Full_Adder full_adder_3 (.A(xor_3_out), .B(1'b0), .Cin(full_adder_4_cout), .Cout(full_adder_3_cout), .S(out_12));
  Full_Adder full_adder_4 (.A(xor_4_out), .B(1'b0), .Cin(full_adder_5_cout), .Cout(full_adder_4_cout), .S(out_13));
  Full_Adder full_adder_5 (.A(xor_5_out), .B(1'b0), .Cin(full_adder_6_cout), .Cout(full_adder_5_cout), .S(out_14));
  Full_Adder full_adder_6 (.A(xor_6_out), .B(1'b0), .Cin(full_adder_7_cout), .Cout(full_adder_6_cout), .S(out_15));
  Full_Adder full_adder_7 (.A(xor_7_out), .B(1'b0), .Cin(full_adder_8_cout), .Cout(full_adder_7_cout), .S(out_16));
  Full_Adder full_adder_8 (.A(xor_8_out), .Cin(in_1), .Cout(full_adder_8_cout), .S(out_17));  // open: B
endmodule
