// Logisim project 8_bit_hardware_multiplier.circ as structural Verilog: 9 circuits, main circuit main
module main (
  input  in_1
);

  wire A0, A1, A2, A3, A4, A5, A6, A7, Add, B0, B1, B2, B3, B4, B5, B6, B7, C, CLK, Done, Enable, LSB, O7,
       O8, O9, O10, O11, O12, O13, O14, Q0, Q1, Q2, Q3, Q4, Q5, Q6, Q7, ripple_carry_adder_1_co,
       ripple_carry_adder_1_s0, ripple_carry_adder_1_s1, ripple_carry_adder_1_s2, ripple_carry_adder_1_s3,
       ripple_carry_adder_1_s4, ripple_carry_adder_1_s5, ripple_carry_adder_1_s6, ripple_carry_adder_1_s7,
       Shift;
  wire [3:0] input_display_1_i0, input_display_1_i1, input_display_1_i2, input_display_2_i0,
       input_display_2_i1, input_display_2_i2, output_display_1_q0, output_display_1_q1, output_display_1_q2,
       output_display_1_q3, output_display_1_q4;
  wire [15:0] R;

  LED led_1 (.in(Done));
  // DipSwitch dipswitch_1: pin names not known
  // DipSwitch dipswitch_2: pin names not known
  Clock clock_1 (.out(CLK));
  Hex_Digit_Display hex_digit_display_1 (.value(input_display_1_i2));  // open: dp
  Hex_Digit_Display hex_digit_display_2 (.value(input_display_2_i2));  // open: dp
  Hex_Digit_Display hex_digit_display_3 (.value(output_display_1_q4));  // open: dp
  Output_Display output_display_1 (
    .A(R), .q4(output_display_1_q4), .q3(output_display_1_q3), .q2(output_display_1_q2),
    .q1(output_display_1_q1), .q0(output_display_1_q0));
  Hex_Digit_Display hex_digit_display_4 (.value(input_display_1_i1));  // open: dp
  Hex_Digit_Display hex_digit_display_5 (.value(input_display_2_i1));  // open: dp
  Hex_Digit_Display hex_digit_display_6 (.value(output_display_1_q3));  // open: dp
  Hex_Digit_Display hex_digit_display_7 (.value(output_display_1_q2));  // open: dp
  Input_Display input_display_1 (
    .I({A7, A6, A5, A4, A3, A2, A1, A0}), .I2(input_display_1_i2), .I1(input_display_1_i1),
    .I0(input_display_1_i0));
  Hex_Digit_Display hex_digit_display_8 (.value(input_display_1_i0));  // open: dp
  Input_Display input_display_2 (
    .I({B7, B6, B5, B4, B3, B2, B1, B0}), .I2(input_display_2_i2), .I1(input_display_2_i1),
    .I0(input_display_2_i0));
  Hex_Digit_Display hex_digit_display_9 (.value(input_display_2_i0));  // open: dp
  Hex_Digit_Display hex_digit_display_10 (.value(output_display_1_q1));  // open: dp
  Hex_Digit_Display hex_digit_display_11 (.value(output_display_1_q0));  // open: dp
  Multiplicand_Register multiplicand_register_1 (
    .CLK(CLK), .Enable(Enable), .I7(A7), .I6(A6), .I5(A5), .I4(A4), .I3(A3), .I2(A2), .I1(A1), .I0(A0),
    .Q7(Q7), .Q6(Q6), .Q5(Q5), .Q4(Q4), .Q3(Q3), .Q2(Q2), .Q1(Q1), .Q0(Q0));
  Multiplier_Register multiplier_register_1 (
    .CLK(CLK), .SHIFT(Shift), .Enable(Enable), .I7(B7), .I6(B6), .I5(B5), .I4(B4), .I3(B3), .I2(B2), .I1(B1),
    .I0(B0), .Q0(LSB));
  Ripple_Carry_Adder ripple_carry_adder_1 (
    .A7(Q7), .B7(O14), .A6(Q6), .B6(O13), .A5(Q5), .B5(O12), .A4(Q4), .B4(O11), .A3(Q3), .B3(O10), .A2(Q2),
    .B2(O9), .A1(Q1), .B1(O8), .A0(Q0), .B0(O7), .Co(ripple_carry_adder_1_co), .S7(ripple_carry_adder_1_s7),
    .S6(ripple_carry_adder_1_s6), .S5(ripple_carry_adder_1_s5), .S4(ripple_carry_adder_1_s4),
    .S3(ripple_carry_adder_1_s3), .S2(ripple_carry_adder_1_s2), .S1(ripple_carry_adder_1_s1),
    .S0(ripple_carry_adder_1_s0));
  FSM fsm_1 (.CLK(CLK), .LSB(LSB), .Start(in_1), .Count_Done(C), .Idle(Enable), .ADD(Add), .SHIFT(Shift), .DONE(Done));
  Accumulator accumulator_1 (
    .CLK(CLK), .Add_Enable(Add), .Shift_Enable(Shift), .V(ripple_carry_adder_1_co),
    .I7(ripple_carry_adder_1_s7), .I6(ripple_carry_adder_1_s6), .I5(ripple_carry_adder_1_s5),
    .I4(ripple_carry_adder_1_s4), .I3(ripple_carry_adder_1_s3), .I2(ripple_carry_adder_1_s2),
    .I1(ripple_carry_adder_1_s1), .I0(ripple_carry_adder_1_s0), .CLR(in_1), .O14(O14), .O13(O13), .O12(O12),
    .O11(O11), .O10(O10), .O9(O9), .O8(O8), .O7(O7), .Result(R));
  Loop_Counter loop_counter_1 (.CLK(CLK), .CLR(in_1), .Shift_Enable(Shift), .count(C));

  // Other names for the same wires on the sheet: Start = in_1
endmodule

module Accumulator (
  input  CLK,
  input  Add_Enable,
  input  Shift_Enable,
  input  V,
  input  I7,
  input  I6,
  input  I5,
  input  I4,
  input  I3,
  input  I2,
  input  I1,
  input  I0,
  input  CLR,
  output O14,
  output O13,
  output O12,
  output O11,
  output O10,
  output O9,
  output O8,
  output O7,
  output [15:0] Result
);

  wire and_1_out, and_2_out, and_3_out, and_4_out, and_5_out, and_6_out, and_7_out, and_8_out, and_9_out,
       and_10_out, and_11_out, and_12_out, and_13_out, and_14_out, and_15_out, and_16_out, and_17_out,
       and_18_out, and_19_out, and_20_out, and_21_out, and_22_out, and_23_out, and_24_out, and_25_out,
       and_26_out, and_27_out, and_28_out, and_29_out, and_30_out, and_31_out, and_32_out, and_33_out,
       and_34_out, and_35_out, and_36_out, and_37_out, and_38_out, and_39_out, and_40_out, not_1_out,
       not_2_out, not_3_out, not_4_out, or_1_out, or_2_out, or_3_out, or_4_out, or_5_out, or_6_out, or_7_out,
       or_8_out, or_9_out, or_10_out, or_11_out, or_12_out, or_13_out, or_14_out, or_15_out, or_16_out;

  not not_1 (not_1_out, CLR);
  not not_2 (not_2_out, Add_Enable);
  not not_3 (not_3_out, Shift_Enable);
  and and_1 (and_1_out, Result[15], not_2_out, not_3_out);
  and and_2 (and_2_out, Add_Enable, not_3_out, V);
  and and_3 (and_3_out, O14, not_3_out, not_2_out);
  and and_4 (and_4_out, not_3_out, Add_Enable, I7);
  and and_5 (and_5_out, Shift_Enable, Result[15]);
  and and_6 (and_6_out, O13, not_3_out, not_2_out);
  and and_7 (and_7_out, not_3_out, Add_Enable, I6);
  and and_8 (and_8_out, Shift_Enable, O14);
  and and_9 (and_9_out, O12, not_3_out, not_2_out);
  and and_10 (and_10_out, not_3_out, Add_Enable, I5);
  and and_11 (and_11_out, Shift_Enable, O13);
  and and_12 (and_12_out, O11, not_3_out, not_2_out);
  and and_13 (and_13_out, not_3_out, Add_Enable, I4);
  and and_14 (and_14_out, Shift_Enable, O12);
  and and_15 (and_15_out, O10, not_3_out, not_2_out);
  and and_16 (and_16_out, not_3_out, Add_Enable, I3);
  and and_17 (and_17_out, Shift_Enable, O11);
  and and_18 (and_18_out, O9, not_3_out, not_2_out);
  and and_19 (and_19_out, not_3_out, Add_Enable, I2);
  and and_20 (and_20_out, Shift_Enable, O10);
  and and_21 (and_21_out, O8, not_3_out, not_2_out);
  and and_22 (and_22_out, not_3_out, Add_Enable, I1);
  and and_23 (and_23_out, Shift_Enable, O9);
  and and_24 (and_24_out, O7, not_3_out, not_2_out);
  and and_25 (and_25_out, not_3_out, Add_Enable, I0);
  and and_26 (and_26_out, Shift_Enable, O8);
  or or_1 (or_1_out, and_1_out, and_2_out);
  or or_2 (or_2_out, and_3_out, and_4_out, and_5_out);
  or or_3 (or_3_out, and_6_out, and_7_out, and_8_out);
  or or_4 (or_4_out, and_9_out, and_10_out, and_11_out);
  or or_5 (or_5_out, and_12_out, and_13_out, and_14_out);
  or or_6 (or_6_out, and_15_out, and_16_out, and_17_out);
  or or_7 (or_7_out, and_18_out, and_19_out, and_20_out);
  or or_8 (or_8_out, and_21_out, and_22_out, and_23_out);
  or or_9 (or_9_out, and_24_out, and_25_out, and_26_out);
  D_Flip_Flop d_ff_1 (.D(or_1_out), .clk(CLK), .Q(Result[15]), .reset(not_1_out));  // open: Qn, preset
  D_Flip_Flop d_ff_2 (.D(or_2_out), .clk(CLK), .Q(O14), .reset(not_1_out));  // open: Qn, preset
  D_Flip_Flop d_ff_3 (.D(or_3_out), .clk(CLK), .Q(O13), .reset(not_1_out));  // open: Qn, preset
  D_Flip_Flop d_ff_4 (.D(or_4_out), .clk(CLK), .Q(O12), .reset(not_1_out));  // open: Qn, preset
  D_Flip_Flop d_ff_5 (.D(or_5_out), .clk(CLK), .Q(O11), .reset(not_1_out));  // open: Qn, preset
  D_Flip_Flop d_ff_6 (.D(or_6_out), .clk(CLK), .Q(O10), .reset(not_1_out));  // open: Qn, preset
  D_Flip_Flop d_ff_7 (.D(or_7_out), .clk(CLK), .Q(O9), .reset(not_1_out));  // open: Qn, preset
  D_Flip_Flop d_ff_8 (.D(or_8_out), .clk(CLK), .Q(O8), .reset(not_1_out));  // open: Qn, preset
  D_Flip_Flop d_ff_9 (.D(or_9_out), .clk(CLK), .Q(O7), .reset(not_1_out));  // open: Qn, preset
  not not_4 (not_4_out, Shift_Enable);
  and and_27 (and_27_out, Shift_Enable, O7);
  and and_28 (and_28_out, not_4_out, Result[6]);
  and and_29 (and_29_out, Result[6], Shift_Enable);
  and and_30 (and_30_out, not_4_out, Result[5]);
  and and_31 (and_31_out, Result[5], Shift_Enable);
  and and_32 (and_32_out, not_4_out, Result[4]);
  and and_33 (and_33_out, Result[4], Shift_Enable);
  and and_34 (and_34_out, not_4_out, Result[3]);
  and and_35 (and_35_out, Result[3], Shift_Enable);
  and and_36 (and_36_out, not_4_out, Result[2]);
  and and_37 (and_37_out, Result[2], Shift_Enable);
  and and_38 (and_38_out, not_4_out, Result[1]);
  and and_39 (and_39_out, Result[1], Shift_Enable);
  and and_40 (and_40_out, not_4_out, Result[0]);
  or or_10 (or_10_out, and_27_out, and_28_out);
  or or_11 (or_11_out, and_29_out, and_30_out);
  or or_12 (or_12_out, and_31_out, and_32_out);
  or or_13 (or_13_out, and_33_out, and_34_out);
  or or_14 (or_14_out, and_35_out, and_36_out);
  or or_15 (or_15_out, and_37_out, and_38_out);
  or or_16 (or_16_out, and_39_out, and_40_out);
  D_Flip_Flop d_ff_10 (.D(or_10_out), .clk(CLK), .Q(Result[6]), .reset(not_1_out));  // open: Qn, preset
  D_Flip_Flop d_ff_11 (.D(or_11_out), .clk(CLK), .Q(Result[5]), .reset(not_1_out));  // open: Qn, preset
  D_Flip_Flop d_ff_12 (.D(or_12_out), .clk(CLK), .Q(Result[4]), .reset(not_1_out));  // open: Qn, preset
  D_Flip_Flop d_ff_13 (.D(or_13_out), .clk(CLK), .Q(Result[3]), .reset(not_1_out));  // open: Qn, preset
  D_Flip_Flop d_ff_14 (.D(or_14_out), .clk(CLK), .Q(Result[2]), .reset(not_1_out));  // open: Qn, preset
  D_Flip_Flop d_ff_15 (.D(or_15_out), .clk(CLK), .Q(Result[1]), .reset(not_1_out));  // open: Qn, preset
  D_Flip_Flop d_ff_16 (.D(or_16_out), .clk(CLK), .Q(Result[0]), .reset(not_1_out));  // open: Qn, preset

  assign Result[14:7] = {O14, O13, O12, O11, O10, O9, O8, O7};
endmodule

module FSM (
  input  CLK,
  input  LSB,
  input  Start,
  input  Count_Done,
  output Idle,
  output ADD,
  output SHIFT,
  output DONE
);

  wire and_1_out, and_2_out, and_3_out, and_4_out, and_5_out, and_6_out, and_7_out, j_k_ff_1_q, j_k_ff_1_qn,
       j_k_ff_2_q, j_k_ff_2_qn, not_1_out, not_2_out, or_1_out, or_2_out, or_3_out;

  not not_1 (not_1_out, Count_Done);
  not not_2 (not_2_out, Start);
  and and_1 (and_1_out, j_k_ff_2_q, not_2_out);
  and and_2 (and_2_out, Start, not_1_out, j_k_ff_1_qn);
  and and_3 (and_3_out, j_k_ff_2_q, Start);
  and and_4 (and_4_out, Start, Count_Done);
  and and_5 (and_5_out, Start, j_k_ff_2_qn);
  and and_6 (and_6_out, not_1_out, Start, j_k_ff_2_qn);
  and and_7 (and_7_out, not_2_out, j_k_ff_1_q);
  or or_1 (or_1_out, and_1_out, and_2_out);
  or or_2 (or_2_out, and_3_out, and_4_out);
  or or_3 (or_3_out, and_6_out, and_7_out);
  J_K_Flip_Flop j_k_ff_1 (
    .J(or_2_out), .K(or_3_out), .clk(CLK), .Q(j_k_ff_1_q), .Qn(j_k_ff_1_qn), .reset(not_2_out));  // open: preset
  J_K_Flip_Flop j_k_ff_2 (
    .J(and_5_out), .K(or_1_out), .clk(CLK), .Q(j_k_ff_2_q), .Qn(j_k_ff_2_qn), .reset(not_2_out));  // open: preset
  and and_8 (ADD, j_k_ff_1_qn, LSB, j_k_ff_2_q);
  and and_9 (Idle, j_k_ff_1_qn, j_k_ff_2_qn);
  and and_10 (SHIFT, j_k_ff_2_qn, j_k_ff_1_q);
  and and_11 (DONE, j_k_ff_2_q, j_k_ff_1_q);
endmodule

module Input_Display (
  input  [7:0] I,
  output [3:0] I2,
  output [3:0] I1,
  output [3:0] I0
);

  wire [7:0] divider_1_out, divider_2_out;
  wire [7:4] divider_1_rem, divider_2_rem, divider_3_rem;

  Divider divider_1 (.a(I), .b(8'ha), .out(divider_1_out), .upper({8{1'b0}}), .rem({divider_1_rem, I0}));
  Divider divider_2 (.a(divider_1_out), .b(8'ha), .out(divider_2_out), .upper({8{1'b0}}), .rem({divider_2_rem, I1}));
  Divider divider_3 (.a(divider_2_out), .b(8'ha), .rem({divider_3_rem, I2}));  // open: out, upper
endmodule

module Output_Display (
  input  [15:0] A,
  output [3:0] q4,
  output [3:0] q3,
  output [3:0] q2,
  output [3:0] q1,
  output [3:0] q0
);

  wire [3:0] divider_5_rem, divider_5_rem_2, divider_5_rem_3;
  wire [15:0] divider_1_out, divider_2_out, divider_3_out, divider_4_out;
  wire [15:4] divider_1_rem, divider_2_rem, divider_3_rem, divider_4_rem;

  Divider #(.width(16)) divider_1 (
    .a(A), .b(16'ha), .out(divider_1_out), .upper({16{1'b0}}), .rem({divider_1_rem, q0}));
  Divider #(.width(16)) divider_2 (
    .a(divider_1_out), .b(16'ha), .out(divider_2_out), .upper({16{1'b0}}), .rem({divider_2_rem, q1}));
  Divider #(.width(16)) divider_3 (
    .a(divider_2_out), .b(16'ha), .out(divider_3_out), .upper({16{1'b0}}), .rem({divider_3_rem, q2}));
  Divider #(.width(16)) divider_4 (
    .a(divider_3_out), .b(16'ha), .out(divider_4_out), .upper({16{1'b0}}), .rem({divider_4_rem, q3}));
  Divider #(.width(16)) divider_5 (
    .a(divider_4_out), .b(16'ha), .upper({16{1'b0}}),
    .rem({divider_5_rem_3, divider_5_rem_2, divider_5_rem, q4}));  // open: out
endmodule

module Multiplicand_Register (
  input  CLK,
  input  Enable,
  input  I7,
  input  I6,
  input  I5,
  input  I4,
  input  I3,
  input  I2,
  input  I1,
  input  I0,
  output Q7,
  output Q6,
  output Q5,
  output Q4,
  output Q3,
  output Q2,
  output Q1,
  output Q0
);

  wire and_1_out, and_2_out, and_3_out, and_4_out, and_5_out, and_6_out, and_7_out, and_8_out, and_9_out,
       and_10_out, and_11_out, and_12_out, and_13_out, and_14_out, and_15_out, and_16_out, not_1_out,
       or_1_out, or_2_out, or_3_out, or_4_out, or_5_out, or_6_out, or_7_out, or_8_out;

  not not_1 (not_1_out, Enable);
  and and_1 (and_1_out, Enable, I7);
  and and_2 (and_2_out, not_1_out, Q7);
  and and_3 (and_3_out, Enable, I6);
  and and_4 (and_4_out, not_1_out, Q6);
  and and_5 (and_5_out, Enable, I5);
  and and_6 (and_6_out, not_1_out, Q5);
  and and_7 (and_7_out, Enable, I4);
  and and_8 (and_8_out, not_1_out, Q4);
  and and_9 (and_9_out, Enable, I3);
  and and_10 (and_10_out, not_1_out, Q3);
  and and_11 (and_11_out, Enable, I2);
  and and_12 (and_12_out, not_1_out, Q2);
  and and_13 (and_13_out, Enable, I1);
  and and_14 (and_14_out, not_1_out, Q1);
  and and_15 (and_15_out, Enable, I0);
  and and_16 (and_16_out, not_1_out, Q0);
  or or_1 (or_1_out, and_1_out, and_2_out);
  or or_2 (or_2_out, and_3_out, and_4_out);
  or or_3 (or_3_out, and_5_out, and_6_out);
  or or_4 (or_4_out, and_7_out, and_8_out);
  or or_5 (or_5_out, and_9_out, and_10_out);
  or or_6 (or_6_out, and_11_out, and_12_out);
  or or_7 (or_7_out, and_13_out, and_14_out);
  or or_8 (or_8_out, and_15_out, and_16_out);
  D_Flip_Flop d_ff_1 (.D(or_1_out), .clk(CLK), .Q(Q7));  // open: Qn, preset, reset
  D_Flip_Flop d_ff_2 (.D(or_2_out), .clk(CLK), .Q(Q6));  // open: Qn, preset, reset
  D_Flip_Flop d_ff_3 (.D(or_3_out), .clk(CLK), .Q(Q5));  // open: Qn, preset, reset
  D_Flip_Flop d_ff_4 (.D(or_4_out), .clk(CLK), .Q(Q4));  // open: Qn, preset, reset
  D_Flip_Flop d_ff_5 (.D(or_5_out), .clk(CLK), .Q(Q3));  // open: Qn, preset, reset
  D_Flip_Flop d_ff_6 (.D(or_6_out), .clk(CLK), .Q(Q2));  // open: Qn, preset, reset
  D_Flip_Flop d_ff_7 (.D(or_7_out), .clk(CLK), .Q(Q1));  // open: Qn, preset, reset
  D_Flip_Flop d_ff_8 (.D(or_8_out), .clk(CLK), .Q(Q0));  // open: Qn, preset, reset
endmodule

module Multiplier_Register (
  input  CLK,
  input  SHIFT,
  input  Enable,
  input  I7,
  input  I6,
  input  I5,
  input  I4,
  input  I3,
  input  I2,
  input  I1,
  input  I0,
  output Q0
);

  wire and_1_out, and_2_out, and_3_out, and_4_out, and_5_out, and_6_out, and_7_out, and_8_out, and_9_out,
       and_10_out, and_11_out, and_12_out, and_13_out, and_14_out, and_15_out, and_16_out, and_17_out,
       and_18_out, and_19_out, and_20_out, and_21_out, and_22_out, and_23_out, and_24_out, d_ff_1_q,
       d_ff_2_q, d_ff_3_q, d_ff_4_q, d_ff_5_q, d_ff_6_q, d_ff_7_q, not_1_out, or_1_out, or_2_out, or_3_out,
       or_4_out, or_5_out, or_6_out, or_7_out, or_8_out, or_9_out;

  or or_1 (or_1_out, SHIFT, Enable);
  not not_1 (not_1_out, or_1_out);
  and and_1 (and_1_out, Enable, I7);
  and and_2 (and_2_out, SHIFT, d_ff_2_q);
  and and_3 (and_3_out, d_ff_1_q, not_1_out);
  D_Flip_Flop d_ff_1 (.D(or_2_out), .clk(CLK), .Q(d_ff_1_q));  // open: Qn, preset, reset
  or or_2 (or_2_out, and_1_out, and_2_out, and_3_out);
  and and_4 (and_4_out, SHIFT, d_ff_1_q);
  and and_5 (and_5_out, Enable, I6);
  and and_6 (and_6_out, d_ff_2_q, not_1_out);
  D_Flip_Flop d_ff_2 (.D(or_3_out), .clk(CLK), .Q(d_ff_2_q));  // open: Qn, preset, reset
  or or_3 (or_3_out, and_4_out, and_5_out, and_6_out);
  and and_7 (and_7_out, SHIFT, d_ff_2_q);
  and and_8 (and_8_out, Enable, I5);
  and and_9 (and_9_out, not_1_out, d_ff_3_q);
  or or_4 (or_4_out, and_7_out, and_8_out, and_9_out);
  D_Flip_Flop d_ff_3 (.D(or_4_out), .clk(CLK), .Q(d_ff_3_q));  // open: Qn, preset, reset
  and and_10 (and_10_out, SHIFT, d_ff_3_q);
  and and_11 (and_11_out, Enable, I4);
  and and_12 (and_12_out, not_1_out, d_ff_4_q);
  or or_5 (or_5_out, and_10_out, and_11_out, and_12_out);
  D_Flip_Flop d_ff_4 (.D(or_5_out), .clk(CLK), .Q(d_ff_4_q));  // open: Qn, preset, reset
  and and_13 (and_13_out, SHIFT, d_ff_4_q);
  and and_14 (and_14_out, Enable, I3);
  and and_15 (and_15_out, not_1_out, d_ff_5_q);
  or or_6 (or_6_out, and_13_out, and_14_out, and_15_out);
  D_Flip_Flop d_ff_5 (.D(or_6_out), .clk(CLK), .Q(d_ff_5_q));  // open: Qn, preset, reset
  and and_16 (and_16_out, SHIFT, d_ff_5_q);
  and and_17 (and_17_out, Enable, I2);
  and and_18 (and_18_out, not_1_out, d_ff_6_q);
  D_Flip_Flop d_ff_6 (.D(or_7_out), .clk(CLK), .Q(d_ff_6_q));  // open: Qn, preset, reset
  or or_7 (or_7_out, and_16_out, and_17_out, and_18_out);
  and and_19 (and_19_out, SHIFT, d_ff_6_q);
  and and_20 (and_20_out, Enable, I1);
  and and_21 (and_21_out, not_1_out, d_ff_7_q);
  or or_8 (or_8_out, and_19_out, and_20_out, and_21_out);
  D_Flip_Flop d_ff_7 (.D(or_8_out), .clk(CLK), .Q(d_ff_7_q));  // open: Qn, preset, reset
  and and_22 (and_22_out, SHIFT, d_ff_7_q);
  and and_23 (and_23_out, Enable, I0);
  and and_24 (and_24_out, not_1_out, Q0);
  or or_9 (or_9_out, and_22_out, and_23_out, and_24_out);
  D_Flip_Flop d_ff_8 (.D(or_9_out), .clk(CLK), .Q(Q0));  // open: Qn, preset, reset
endmodule

module Ripple_Carry_Adder (
  input  A7,
  input  B7,
  input  A6,
  input  B6,
  input  A5,
  input  B5,
  input  A4,
  input  B4,
  input  A3,
  input  B3,
  input  A2,
  input  B2,
  input  A1,
  input  B1,
  input  A0,
  input  B0,
  output Co,
  output S7,
  output S6,
  output S5,
  output S4,
  output S3,
  output S2,
  output S1,
  output S0
);

  wire and_1_out, and_2_out, and_3_out, and_4_out, and_5_out, and_6_out, and_7_out, and_8_out, and_9_out,
       and_10_out, and_11_out, and_12_out, and_13_out, and_14_out, and_15_out, and_16_out, and_17_out,
       and_18_out, and_19_out, and_20_out, and_21_out, and_22_out, and_23_out, and_24_out, or_2_out,
       or_3_out, or_4_out, or_5_out, or_6_out, or_7_out, or_8_out, xor_1_out, xor_2_out, xor_3_out,
       xor_4_out, xor_5_out, xor_6_out, xor_7_out, xor_8_out;

  xor xor_1 (xor_1_out, A7, B7);
  xor xor_2 (xor_2_out, A6, B6);
  xor xor_3 (xor_3_out, A5, B5);
  xor xor_4 (xor_4_out, A4, B4);
  xor xor_5 (xor_5_out, A3, B3);
  xor xor_6 (xor_6_out, A2, B2);
  xor xor_7 (xor_7_out, A1, B1);
  xor xor_8 (xor_8_out, A0, B0);
  and and_1 (and_1_out, A7, B7);
  and and_2 (and_2_out, A7, or_2_out);
  and and_3 (and_3_out, B7, or_2_out);
  and and_4 (and_4_out, A6, B6);
  and and_5 (and_5_out, A6, or_3_out);
  and and_6 (and_6_out, B6, or_3_out);
  and and_7 (and_7_out, A5, B5);
  and and_8 (and_8_out, A5, or_4_out);
  and and_9 (and_9_out, B5, or_4_out);
  and and_10 (and_10_out, A4, B4);
  and and_11 (and_11_out, A4, or_5_out);
  and and_12 (and_12_out, B4, or_5_out);
  and and_13 (and_13_out, A3, B3);
  and and_14 (and_14_out, A3, or_6_out);
  and and_15 (and_15_out, B3, or_6_out);
  and and_16 (and_16_out, A2, B2);
  and and_17 (and_17_out, A2, or_7_out);
  and and_18 (and_18_out, B2, or_7_out);
  and and_19 (and_19_out, A1, B1);
  and and_20 (and_20_out, A1, or_8_out);
  and and_21 (and_21_out, B1, or_8_out);
  and and_22 (and_22_out, A0, B0);
  and and_23 (and_23_out, A0, 1'b0);
  and and_24 (and_24_out, B0, 1'b0);
  or or_1 (Co, and_1_out, and_2_out, and_3_out);
  xor xor_9 (S7, xor_1_out, or_2_out);
  or or_2 (or_2_out, and_4_out, and_5_out, and_6_out);
  xor xor_10 (S6, xor_2_out, or_3_out);
  or or_3 (or_3_out, and_7_out, and_8_out, and_9_out);
  xor xor_11 (S5, xor_3_out, or_4_out);
  or or_4 (or_4_out, and_10_out, and_11_out, and_12_out);
  xor xor_12 (S4, xor_4_out, or_5_out);
  or or_5 (or_5_out, and_13_out, and_14_out, and_15_out);
  xor xor_13 (S3, xor_5_out, or_6_out);
  or or_6 (or_6_out, and_16_out, and_17_out, and_18_out);
  xor xor_14 (S2, xor_6_out, or_7_out);
  or or_7 (or_7_out, and_19_out, and_20_out, and_21_out);
  xor xor_15 (S1, xor_7_out, or_8_out);
  or or_8 (or_8_out, and_22_out, and_23_out, and_24_out);
  xor xor_16 (S0, xor_8_out, 1'b0);
endmodule

module Loop_Counter (
  input  CLK,
  input  CLR,
  input  Shift_Enable,
  output count
);

  wire and_1_out, and_2_out, d_ff_1_q, d_ff_2_q, d_ff_3_q, not_1_out, xor_1_out, xor_2_out, xor_3_out;

  not not_1 (not_1_out, CLR);
  and and_1 (and_1_out, d_ff_2_q, d_ff_3_q, Shift_Enable);
  and and_2 (and_2_out, d_ff_3_q, Shift_Enable);
  xor xor_1 (xor_1_out, and_1_out, d_ff_1_q);
  xor xor_2 (xor_2_out, and_2_out, d_ff_2_q);
  xor xor_3 (xor_3_out, Shift_Enable, d_ff_3_q);
  D_Flip_Flop d_ff_1 (.D(xor_1_out), .clk(CLK), .Q(d_ff_1_q), .reset(not_1_out));  // open: Qn, preset
  D_Flip_Flop d_ff_2 (.D(xor_2_out), .clk(CLK), .Q(d_ff_2_q), .reset(not_1_out));  // open: Qn, preset
  D_Flip_Flop d_ff_3 (.D(xor_3_out), .clk(CLK), .Q(d_ff_3_q), .reset(not_1_out));  // open: Qn, preset
  and and_3 (count, d_ff_1_q, d_ff_2_q, d_ff_3_q);
endmodule
