// Logisim project 8_bit_register_file.circ as structural Verilog: 6 circuits, main circuit main
module main (
  input  in_1,
  input  in_2,
  input  in_3,
  input  in_4,
  input  in_5,
  input  in_6,
  input  in_7,
  input  in_8,
  input  in_9,
  input  in_10
);

  wire address_decoder_1_out_6, address_decoder_1_out_7, address_decoder_1_out_8, address_decoder_1_out_9,
       address_decoder_1_out_10, address_decoder_1_out_11, address_decoder_1_out_12,
       address_decoder_1_out_13, address_decoder_1_out_14, address_decoder_1_out_15,
       address_decoder_1_out_16, address_decoder_1_out_17, address_decoder_1_out_18,
       address_decoder_1_out_19, address_decoder_1_out_20, address_decoder_1_out_21, clock_1_out;
  wire [3:0] display_1_out_2, display_1_out_3, display_1_out_4, display_2_out_2, display_2_out_3,
       display_2_out_4;
  wire [7:0] R, register_bank_1_out_19, register_bank_1_out_20, register_bank_1_out_21,
       register_bank_1_out_22, register_bank_1_out_23, register_bank_1_out_24, register_bank_1_out_25,
       register_bank_1_out_26, register_bank_1_out_27, register_bank_1_out_28, register_bank_1_out_29,
       register_bank_1_out_30, register_bank_1_out_31, register_bank_1_out_32, register_bank_1_out_33,
       register_bank_1_out_34, undriven;

  // DipSwitch dipswitch_1: pin names not known
  Hex_Digit_Display hex_digit_display_1 (.value(display_1_out_2));  // open: dp
  Hex_Digit_Display hex_digit_display_2 (.value(display_1_out_3));  // open: dp
  Hex_Digit_Display hex_digit_display_3 (.value(display_2_out_2));  // open: dp
  Hex_Digit_Display hex_digit_display_4 (.value(display_1_out_4));  // open: dp
  Display display_1 (.in_1(undriven), .out_2(display_1_out_2), .out_3(display_1_out_3), .out_4(display_1_out_4));
  Hex_Digit_Display hex_digit_display_5 (.value(display_2_out_3));  // open: dp
  Display display_2 (.in_1(R), .out_2(display_2_out_2), .out_3(display_2_out_3), .out_4(display_2_out_4));
  Hex_Digit_Display hex_digit_display_6 (.value(display_2_out_4));  // open: dp
  Clock clock_1 (.out(clock_1_out));
  Address_Decoder address_decoder_1 (
    .E(in_5), .A3(in_1), .A2(in_2), .A1(in_3), .A0(in_4), .out_6(address_decoder_1_out_6),
    .out_7(address_decoder_1_out_7), .out_8(address_decoder_1_out_8), .out_9(address_decoder_1_out_9),
    .out_10(address_decoder_1_out_10), .out_11(address_decoder_1_out_11), .out_12(address_decoder_1_out_12),
    .out_13(address_decoder_1_out_13), .out_14(address_decoder_1_out_14), .out_15(address_decoder_1_out_15),
    .out_16(address_decoder_1_out_16), .out_17(address_decoder_1_out_17), .out_18(address_decoder_1_out_18),
    .out_19(address_decoder_1_out_19), .out_20(address_decoder_1_out_20), .out_21(address_decoder_1_out_21));
  Register_Bank register_bank_1 (
    .CLK(clock_1_out), .I(undriven), .E0(address_decoder_1_out_6), .E1(address_decoder_1_out_7),
    .E2(address_decoder_1_out_8), .E3(address_decoder_1_out_9), .E4(address_decoder_1_out_10),
    .E5(address_decoder_1_out_11), .E6(address_decoder_1_out_12), .E7(address_decoder_1_out_13),
    .E8(address_decoder_1_out_14), .E9(address_decoder_1_out_15), .E10(address_decoder_1_out_16),
    .E11(address_decoder_1_out_17), .E12(address_decoder_1_out_18), .E13(address_decoder_1_out_19),
    .E14(address_decoder_1_out_20), .E15(address_decoder_1_out_21), .out_19(register_bank_1_out_19),
    .out_20(register_bank_1_out_20), .out_21(register_bank_1_out_21), .out_22(register_bank_1_out_22),
    .out_23(register_bank_1_out_23), .out_24(register_bank_1_out_24), .out_25(register_bank_1_out_25),
    .out_26(register_bank_1_out_26), .out_27(register_bank_1_out_27), .out_28(register_bank_1_out_28),
    .out_29(register_bank_1_out_29), .out_30(register_bank_1_out_30), .out_31(register_bank_1_out_31),
    .out_32(register_bank_1_out_32), .out_33(register_bank_1_out_33), .out_34(register_bank_1_out_34));
  Read_Mux read_mux_1 (
    .E(in_10), .s3(in_6), .s2(in_7), .s1(in_8), .s0(in_9), .I0(register_bank_1_out_19),
    .I1(register_bank_1_out_20), .I2(register_bank_1_out_21), .I3(register_bank_1_out_22),
    .I4(register_bank_1_out_23), .I5(register_bank_1_out_24), .I6(register_bank_1_out_25),
    .I7(register_bank_1_out_26), .I8(register_bank_1_out_27), .I9(register_bank_1_out_28),
    .I10(register_bank_1_out_29), .I11(register_bank_1_out_30), .I12(register_bank_1_out_31),
    .I13(register_bank_1_out_32), .I14(register_bank_1_out_33), .I15(register_bank_1_out_34), .R(R));

  // Other names for the same wires on the sheet: r_t = in_10; s0 = in_9; s1 = in_8; s2 = in_7; s3 = in_6; w = in_5

  // Notes on the sheet:
  //   INPUT
  //   Input Address
  //   Write
  //   Output Address
  //   Read
endmodule

module Input_Register (
  input  CLK,
  input  Enable,
  input  [7:0] in_3,
  output [7:0] out_4
);

  wire and_1_out, and_2_out, and_3_out, and_4_out, and_5_out, and_6_out, and_7_out, and_8_out, and_9_out,
       and_10_out, and_11_out, and_12_out, and_13_out, and_14_out, and_15_out, and_16_out, not_1_out,
       or_1_out, or_2_out, or_3_out, or_4_out, or_5_out, or_6_out, or_7_out, or_8_out;

  not not_1 (not_1_out, Enable);
  and and_1 (and_1_out, out_4[7], not_1_out);
  and and_2 (and_2_out, Enable, in_3[7]);
  and and_3 (and_3_out, out_4[6], not_1_out);
  and and_4 (and_4_out, Enable, in_3[6]);
  and and_5 (and_5_out, out_4[5], not_1_out);
  and and_6 (and_6_out, Enable, in_3[5]);
  and and_7 (and_7_out, out_4[4], not_1_out);
  and and_8 (and_8_out, Enable, in_3[4]);
  and and_9 (and_9_out, out_4[3], not_1_out);
  and and_10 (and_10_out, Enable, in_3[3]);
  and and_11 (and_11_out, out_4[2], not_1_out);
  and and_12 (and_12_out, Enable, in_3[2]);
  and and_13 (and_13_out, out_4[1], not_1_out);
  and and_14 (and_14_out, Enable, in_3[1]);
  and and_15 (and_15_out, out_4[0], not_1_out);
  and and_16 (and_16_out, Enable, in_3[0]);
  D_Flip_Flop d_ff_1 (.D(or_1_out), .clk(CLK), .Q(out_4[7]));  // open: Qn, preset, reset
  or or_1 (or_1_out, and_1_out, and_2_out);
  D_Flip_Flop d_ff_2 (.D(or_2_out), .clk(CLK), .Q(out_4[6]));  // open: Qn, preset, reset
  or or_2 (or_2_out, and_3_out, and_4_out);
  D_Flip_Flop d_ff_3 (.D(or_3_out), .clk(CLK), .Q(out_4[5]));  // open: Qn, preset, reset
  or or_3 (or_3_out, and_5_out, and_6_out);
  D_Flip_Flop d_ff_4 (.D(or_4_out), .clk(CLK), .Q(out_4[4]));  // open: Qn, preset, reset
  or or_4 (or_4_out, and_7_out, and_8_out);
  D_Flip_Flop d_ff_5 (.D(or_5_out), .clk(CLK), .Q(out_4[3]));  // open: Qn, preset, reset
  or or_5 (or_5_out, and_9_out, and_10_out);
  D_Flip_Flop d_ff_6 (.D(or_6_out), .clk(CLK), .Q(out_4[2]));  // open: Qn, preset, reset
  or or_6 (or_6_out, and_11_out, and_12_out);
  D_Flip_Flop d_ff_7 (.D(or_7_out), .clk(CLK), .Q(out_4[1]));  // open: Qn, preset, reset
  or or_7 (or_7_out, and_13_out, and_14_out);
  D_Flip_Flop d_ff_8 (.D(or_8_out), .clk(CLK), .Q(out_4[0]));  // open: Qn, preset, reset
  or or_8 (or_8_out, and_15_out, and_16_out);
endmodule

module Register_Bank (
  input  CLK,
  input  [7:0] I,
  input  E0,
  input  E1,
  input  E2,
  input  E3,
  input  E4,
  input  E5,
  input  E6,
  input  E7,
  input  E8,
  input  E9,
  input  E10,
  input  E11,
  input  E12,
  input  E13,
  input  E14,
  input  E15,
  output [7:0] out_19,
  output [7:0] out_20,
  output [7:0] out_21,
  output [7:0] out_22,
  output [7:0] out_23,
  output [7:0] out_24,
  output [7:0] out_25,
  output [7:0] out_26,
  output [7:0] out_27,
  output [7:0] out_28,
  output [7:0] out_29,
  output [7:0] out_30,
  output [7:0] out_31,
  output [7:0] out_32,
  output [7:0] out_33,
  output [7:0] out_34
);

  Input_Register R0 (.CLK(CLK), .Enable(E0), .in_3(I), .out_4(out_19));
  Input_Register R4 (.CLK(CLK), .Enable(E4), .in_3(I), .out_4(out_23));
  Input_Register R8 (.CLK(CLK), .Enable(E8), .in_3(I), .out_4(out_27));
  Input_Register R12 (.CLK(CLK), .Enable(E12), .in_3(I), .out_4(out_31));
  Input_Register R1 (.CLK(CLK), .Enable(E1), .in_3(I), .out_4(out_20));
  Input_Register R5 (.CLK(CLK), .Enable(E5), .in_3(I), .out_4(out_24));
  Input_Register R9 (.CLK(CLK), .Enable(E9), .in_3(I), .out_4(out_28));
  Input_Register R13 (.CLK(CLK), .Enable(E13), .in_3(I), .out_4(out_32));
  Input_Register R2 (.CLK(CLK), .Enable(E2), .in_3(I), .out_4(out_21));
  Input_Register R6 (.CLK(CLK), .Enable(E6), .in_3(I), .out_4(out_25));
  Input_Register R10 (.CLK(CLK), .Enable(E10), .in_3(I), .out_4(out_29));
  Input_Register R14 (.CLK(CLK), .Enable(E14), .in_3(I), .out_4(out_33));
  Input_Register R3 (.CLK(CLK), .Enable(E3), .in_3(I), .out_4(out_22));
  Input_Register R7 (.CLK(CLK), .Enable(E7), .in_3(I), .out_4(out_26));
  Input_Register R11 (.CLK(CLK), .Enable(E11), .in_3(I), .out_4(out_30));
  Input_Register R15 (.CLK(CLK), .Enable(E15), .in_3(I), .out_4(out_34));

  // Other names for the same wires on the sheet: O0[7:0] = out_19; O1[7:0] = out_20; O2[7:0] = out_21;
  //   O3[7:0] = out_22; O4[7:0] = out_23; O5[7:0] = out_24; O6[7:0] = out_25; O7[7:0] = out_26; O8[7:0] = out_27;
  //   O9[7:0] = out_28; O10[7:0] = out_29; O11[7:0] = out_30; O12[7:0] = out_31; O13[7:0] = out_32; O14[7:0] = out_33;
  //   O15[7:0] = out_34
endmodule

module Address_Decoder (
  input  E,
  input  A3,
  input  A2,
  input  A1,
  input  A0,
  output out_6,
  output out_7,
  output out_8,
  output out_9,
  output out_10,
  output out_11,
  output out_12,
  output out_13,
  output out_14,
  output out_15,
  output out_16,
  output out_17,
  output out_18,
  output out_19,
  output out_20,
  output out_21
);

  wire and_1_out, and_2_out, and_3_out, and_4_out, and_5_out, and_6_out, and_7_out, and_8_out, and_9_out,
       and_10_out, and_11_out, and_12_out, and_13_out, and_14_out, and_15_out, and_16_out, not_1_out,
       not_2_out, not_3_out, not_4_out;

  not not_1 (not_1_out, A3);
  not not_2 (not_2_out, A2);
  not not_3 (not_3_out, A1);
  not not_4 (not_4_out, A0);
  and and_1 (and_1_out, not_1_out, not_2_out, not_3_out, not_4_out);
  and and_2 (and_2_out, not_1_out, not_2_out, not_3_out, A0);
  and and_3 (and_3_out, not_1_out, not_2_out, A1, not_4_out);
  and and_4 (and_4_out, not_1_out, not_2_out, A1, A0);
  and and_5 (and_5_out, not_1_out, A2, not_3_out, not_4_out);
  and and_6 (and_6_out, not_1_out, A2, not_3_out, A0);
  and and_7 (and_7_out, not_1_out, A2, A1, not_4_out);
  and and_8 (and_8_out, not_1_out, A2, A1, A0);
  and and_9 (and_9_out, A3, not_2_out, not_3_out, not_4_out);
  and and_10 (and_10_out, A3, not_2_out, not_3_out, A0);
  and and_11 (and_11_out, A3, not_2_out, A1, not_4_out);
  and and_12 (and_12_out, A3, not_2_out, A1, A0);
  and and_13 (and_13_out, A3, A2, not_3_out, not_4_out);
  and and_14 (and_14_out, A3, A2, not_3_out, A0);
  and and_15 (and_15_out, A3, A2, A1, not_4_out);
  and and_16 (and_16_out, A3, A2, A1, A0);
  and and_17 (out_6, E, and_1_out);
  and and_18 (out_7, E, and_2_out);
  and and_19 (out_8, E, and_3_out);
  and and_20 (out_9, E, and_4_out);
  and and_21 (out_10, E, and_5_out);
  and and_22 (out_11, E, and_6_out);
  and and_23 (out_12, E, and_7_out);
  and and_24 (out_13, E, and_8_out);
  and and_25 (out_14, E, and_9_out);
  and and_26 (out_15, E, and_10_out);
  and and_27 (out_16, E, and_11_out);
  and and_28 (out_17, E, and_12_out);
  and and_29 (out_18, E, and_13_out);
  and and_30 (out_19, E, and_14_out);
  and and_31 (out_20, E, and_15_out);
  and and_32 (out_21, E, and_16_out);
endmodule

module Read_Mux (
  input  E,
  input  s3,
  input  s2,
  input  s1,
  input  s0,
  input  [7:0] I0,
  input  [7:0] I1,
  input  [7:0] I2,
  input  [7:0] I3,
  input  [7:0] I4,
  input  [7:0] I5,
  input  [7:0] I6,
  input  [7:0] I7,
  input  [7:0] I8,
  input  [7:0] I9,
  input  [7:0] I10,
  input  [7:0] I11,
  input  [7:0] I12,
  input  [7:0] I13,
  input  [7:0] I14,
  input  [7:0] I15,
  output [7:0] R
);

  wire R0, R1, R2, R3, R4, R5, R6, R7, R8, R9, R10, R11, R12, R13, R14, R15;
  wire [7:0] O0, O1, O2, O3, O4, O5, O6, O7, O8, O9, O10, O11, O12, O13, O14, O15;

  and and_1 (O0[7], I0[7], R0);
  and and_2 (O0[6], I0[6], R0);
  and and_3 (O0[5], I0[5], R0);
  and and_4 (O0[4], I0[4], R0);
  and and_5 (O0[3], R0, I0[3]);
  and and_6 (O0[2], R0, I0[2]);
  and and_7 (O0[1], R0, I0[1]);
  and and_8 (O0[0], R0, I0[0]);
  and and_9 (O4[7], I4[7], R4);
  and and_10 (O4[6], I4[6], R4);
  and and_11 (O4[5], I4[5], R4);
  and and_12 (O4[4], I4[4], R4);
  and and_13 (O4[3], R4, I4[3]);
  and and_14 (O4[2], R4, I4[2]);
  and and_15 (O4[1], R4, I4[1]);
  and and_16 (O4[0], R4, I4[0]);
  and and_17 (O8[7], I8[7], R8);
  and and_18 (O8[6], I8[6], R8);
  and and_19 (O8[5], I8[5], R8);
  and and_20 (O8[4], I8[4], R8);
  and and_21 (O8[3], R8, I8[3]);
  and and_22 (O8[2], R8, I8[2]);
  and and_23 (O8[1], R8, I8[1]);
  and and_24 (O8[0], R8, I8[0]);
  and and_25 (O12[7], I12[7], R12);
  and and_26 (O12[6], I12[6], R12);
  and and_27 (O12[5], I12[5], R12);
  and and_28 (O12[4], I12[4], R12);
  and and_29 (O12[3], R12, I12[3]);
  and and_30 (O12[2], R12, I12[2]);
  and and_31 (O12[1], R12, I12[1]);
  and and_32 (O12[0], R12, I12[0]);
  Address_Decoder address_decoder_1 (
    .E(E), .A3(s3), .A2(s2), .A1(s1), .A0(s0), .out_6(R0), .out_7(R1), .out_8(R2), .out_9(R3), .out_10(R4),
    .out_11(R5), .out_12(R6), .out_13(R7), .out_14(R8), .out_15(R9), .out_16(R10), .out_17(R11),
    .out_18(R12), .out_19(R13), .out_20(R14), .out_21(R15));
  and and_33 (O1[7], I1[7], R1);
  and and_34 (O1[6], I1[6], R1);
  and and_35 (O1[5], I1[5], R1);
  and and_36 (O1[4], I1[4], R1);
  and and_37 (O1[3], R1, I1[3]);
  and and_38 (O1[2], R1, I1[2]);
  and and_39 (O1[1], R1, I1[1]);
  and and_40 (O1[0], R1, I1[0]);
  and and_41 (O5[7], I5[7], R5);
  and and_42 (O5[6], I5[6], R5);
  and and_43 (O5[5], I5[5], R5);
  and and_44 (O5[4], I5[4], R5);
  and and_45 (O5[3], R5, I5[3]);
  and and_46 (O5[2], R5, I5[2]);
  and and_47 (O5[1], R5, I5[1]);
  and and_48 (O5[0], R5, I5[0]);
  and and_49 (O9[7], I9[7], R9);
  and and_50 (O9[6], I9[6], R9);
  and and_51 (O9[5], I9[5], R9);
  and and_52 (O9[4], I9[4], R9);
  and and_53 (O9[3], R9, I9[3]);
  and and_54 (O9[2], R9, I9[2]);
  and and_55 (O9[1], R9, I9[1]);
  and and_56 (O9[0], R9, I9[0]);
  and and_57 (O13[7], I13[7], R13);
  and and_58 (O13[6], I13[6], R13);
  and and_59 (O13[5], I13[5], R13);
  and and_60 (O13[4], I13[4], R13);
  and and_61 (O13[3], R13, I13[3]);
  and and_62 (O13[2], R13, I13[2]);
  and and_63 (O13[1], R13, I13[1]);
  and and_64 (O13[0], R13, I13[0]);
  and and_65 (O2[7], I2[7], R2);
  and and_66 (O2[6], I2[6], R2);
  and and_67 (O2[5], I2[5], R2);
  and and_68 (O2[4], I2[4], R2);
  and and_69 (O2[3], R2, I2[3]);
  and and_70 (O2[2], R2, I2[2]);
  and and_71 (O2[1], R2, I2[1]);
  and and_72 (O2[0], R2, I2[0]);
  and and_73 (O6[7], I6[7], R6);
  and and_74 (O6[6], I6[6], R6);
  and and_75 (O6[5], I6[5], R6);
  and and_76 (O6[4], I6[4], R6);
  and and_77 (O6[3], R6, I6[3]);
  and and_78 (O6[2], R6, I6[2]);
  and and_79 (O6[1], R6, I6[1]);
  and and_80 (O6[0], R6, I6[0]);
  and and_81 (O10[7], I10[7], R10);
  and and_82 (O10[6], I10[6], R10);
  and and_83 (O10[5], I10[5], R10);
  and and_84 (O10[4], I10[4], R10);
  and and_85 (O10[3], R10, I10[3]);
  and and_86 (O10[2], R10, I10[2]);
  and and_87 (O10[1], R10, I10[1]);
  and and_88 (O10[0], R10, I10[0]);
  and and_89 (O14[7], I14[7], R14);
  and and_90 (O14[6], I14[6], R14);
  and and_91 (O14[5], I14[5], R14);
  and and_92 (O14[4], I14[4], R14);
  and and_93 (O14[3], R14, I14[3]);
  and and_94 (O14[2], R14, I14[2]);
  and and_95 (O14[1], R14, I14[1]);
  and and_96 (O14[0], R14, I14[0]);
  and and_97 (O3[7], I3[7], R3);
  and and_98 (O3[6], I3[6], R3);
  and and_99 (O3[5], I3[5], R3);
  and and_100 (O3[4], I3[4], R3);
  and and_101 (O3[3], R3, I3[3]);
  and and_102 (O3[2], R3, I3[2]);
  and and_103 (O3[1], R3, I3[1]);
  and and_104 (O3[0], R3, I3[0]);
  and and_105 (O7[7], I7[7], R7);
  and and_106 (O7[6], I7[6], R7);
  and and_107 (O7[5], I7[5], R7);
  and and_108 (O7[4], I7[4], R7);
  and and_109 (O7[3], R7, I7[3]);
  and and_110 (O7[2], R7, I7[2]);
  and and_111 (O7[1], R7, I7[1]);
  and and_112 (O7[0], R7, I7[0]);
  and and_113 (O11[7], I11[7], R11);
  and and_114 (O11[6], I11[6], R11);
  and and_115 (O11[5], I11[5], R11);
  and and_116 (O11[4], I11[4], R11);
  and and_117 (O11[3], R11, I11[3]);
  and and_118 (O11[2], R11, I11[2]);
  and and_119 (O11[1], R11, I11[1]);
  and and_120 (O11[0], R11, I11[0]);
  and and_121 (O15[7], I15[7], R15);
  and and_122 (O15[6], I15[6], R15);
  and and_123 (O15[5], I15[5], R15);
  and and_124 (O15[4], I15[4], R15);
  and and_125 (O15[3], R15, I15[3]);
  and and_126 (O15[2], R15, I15[2]);
  and and_127 (O15[1], R15, I15[1]);
  and and_128 (O15[0], R15, I15[0]);
  assign R = O0 | O1 | O2 | O3 | O4 | O5 | O6 | O7 | O8 | O9 | O10 | O11 | O12 | O13 | O14 | O15;  // OR_Gate or_1, 8 bits wide
endmodule

module Display (
  input  [7:0] in_1,
  output [3:0] out_2,
  output [3:0] out_3,
  output [3:0] out_4
);

  wire [7:0] divider_1_out, divider_2_out;
  wire [7:4] divider_1_rem, divider_2_rem, divider_3_rem;

  Divider divider_1 (.a(in_1), .b(8'ha), .out(divider_1_out), .upper({8{1'b0}}), .rem({divider_1_rem, out_4}));
  Divider divider_2 (.a(divider_1_out), .b(8'ha), .out(divider_2_out), .upper({8{1'b0}}), .rem({divider_2_rem, out_3}));
  Divider divider_3 (.a(divider_2_out), .b(8'ha), .upper({8{1'b0}}), .rem({divider_3_rem, out_2}));  // open: out
endmodule
