// Logisim project 8_bit_program_counter.circ as structural Verilog: 7 circuits, main circuit main
module main (
  input  in_1,
  input  in_2,
  input  HOLD,
  input  in_4
);

  wire clock_1_out, priority_control_1_out_5, priority_control_1_out_6;
  wire [3:0] display_1_out_2, display_1_out_3, display_1_out_4;
  wire [7:0] H, I, L, pc_mux_1_out_6;

  // DipSwitch dipswitch_1: pin names not known
  priority_control priority_control_1 (
    .reset(in_1), .load(in_2), .hold(HOLD), .enable(in_4), .out_5(priority_control_1_out_5),
    .out_6(priority_control_1_out_6));
  Hex_Digit_Display hex_digit_display_1 (.value(display_1_out_2));  // open: dp
  Clock clock_1 (.out(clock_1_out));
  pc_mux pc_mux_1 (
    .s1(priority_control_1_out_5), .s0(priority_control_1_out_6), .load(L), .hold(H), .increment(I),
    .out_6(pc_mux_1_out_6));
  Hex_Digit_Display hex_digit_display_2 (.value(display_1_out_3));  // open: dp
  display display_1 (.in_1(H), .out_2(display_1_out_2), .out_3(display_1_out_3), .out_4(display_1_out_4));
  Hex_Digit_Display hex_digit_display_3 (.value(display_1_out_4));  // open: dp
  pc_register pc_register_1 (
    .clk(clock_1_out), .reset(in_1), .in_3(pc_mux_1_out_6), .q7(H[7]), .q6(H[6]), .q5(H[5]), .q4(H[4]),
    .q3(H[3]), .q2(H[2]), .q1(H[1]), .q0(H[0]));
  incrementer incrementer_1 (
    .in_1(H[7]), .in_2(H[6]), .in_3(H[5]), .in_4(H[4]), .in_5(H[3]), .in_6(H[2]), .in_7(H[1]), .in_8(H[0]),
    .out_9(I[7]), .out_10(I[6]), .out_11(I[5]), .out_12(I[4]), .out_13(I[3]), .out_14(I[2]), .out_15(I[1]),
    .out_16(I[0]));

  // Notes on the sheet:
  //   RESET
  //   LOAD
  //   INCREMENT
  //   Load_Input
endmodule

module pc_register (
  input  clk,
  input  reset,
  input  [7:0] in_3,
  output q7,
  output q6,
  output q5,
  output q4,
  output q3,
  output q2,
  output q1,
  output q0
);

  D_Flip_Flop d_ff_1 (.D(in_3[7]), .clk(clk), .Q(q7), .reset(reset));  // open: Qn, preset
  D_Flip_Flop d_ff_2 (.D(in_3[6]), .clk(clk), .Q(q6), .reset(reset));  // open: Qn, preset
  D_Flip_Flop d_ff_3 (.D(in_3[5]), .clk(clk), .Q(q5), .reset(reset));  // open: Qn, preset
  D_Flip_Flop d_ff_4 (.D(in_3[4]), .clk(clk), .Q(q4), .reset(reset));  // open: Qn, preset
  D_Flip_Flop d_ff_5 (.D(in_3[3]), .clk(clk), .Q(q3), .reset(reset));  // open: Qn, preset
  D_Flip_Flop d_ff_6 (.D(in_3[2]), .clk(clk), .Q(q2), .reset(reset));  // open: Qn, preset
  D_Flip_Flop d_ff_7 (.D(in_3[1]), .clk(clk), .Q(q1), .reset(reset));  // open: Qn, preset
  D_Flip_Flop d_ff_8 (.D(in_3[0]), .clk(clk), .Q(q0), .reset(reset));  // open: Qn, preset
endmodule

module incrementer (
  input  in_1,
  input  in_2,
  input  in_3,
  input  in_4,
  input  in_5,
  input  in_6,
  input  in_7,
  input  in_8,
  output out_9,
  output out_10,
  output out_11,
  output out_12,
  output out_13,
  output out_14,
  output out_15,
  output out_16
);

  wire full_adder_2_cout, full_adder_3_cout, full_adder_4_cout, full_adder_5_cout, full_adder_6_cout,
       full_adder_7_cout, full_adder_8_cout;

  full_adder full_adder_1 (.A(in_1), .B(1'b0), .Cin(full_adder_2_cout), .S(out_9));  // open: Cout
  full_adder full_adder_2 (.A(in_2), .B(1'b0), .Cin(full_adder_3_cout), .Cout(full_adder_2_cout), .S(out_10));
  full_adder full_adder_3 (.A(in_3), .B(1'b0), .Cin(full_adder_4_cout), .Cout(full_adder_3_cout), .S(out_11));
  full_adder full_adder_4 (.A(in_4), .B(1'b0), .Cin(full_adder_5_cout), .Cout(full_adder_4_cout), .S(out_12));
  full_adder full_adder_5 (.A(in_5), .B(1'b0), .Cin(full_adder_6_cout), .Cout(full_adder_5_cout), .S(out_13));
  full_adder full_adder_6 (.A(in_6), .B(1'b0), .Cin(full_adder_7_cout), .Cout(full_adder_6_cout), .S(out_14));
  full_adder full_adder_7 (.A(in_7), .B(1'b0), .Cin(full_adder_8_cout), .Cout(full_adder_7_cout), .S(out_15));
  full_adder full_adder_8 (.A(in_8), .B(1'b1), .Cin(1'b0), .Cout(full_adder_8_cout), .S(out_16));
endmodule

module pc_mux (
  input  s1,
  input  s0,
  input  [7:0] load,
  input  [7:0] hold,
  input  [7:0] increment,
  output [7:0] out_6
);

  wire and_1_out, and_2_out, and_3_out, not_1_out, not_2_out;
  wire [7:0] H, I, L;

  not not_1 (not_1_out, s0);
  not not_2 (not_2_out, s1);
  and and_1 (and_1_out, s1, s0);
  and and_2 (and_2_out, s1, not_1_out);
  and and_3 (and_3_out, not_2_out, s0);
  and and_4 (L[7], and_3_out, load[7]);
  and and_5 (L[6], and_3_out, load[6]);
  and and_6 (L[5], and_3_out, load[5]);
  and and_7 (L[4], and_3_out, load[4]);
  and and_8 (L[3], load[3], and_3_out);
  and and_9 (L[2], load[2], and_3_out);
  and and_10 (L[1], load[1], and_3_out);
  and and_11 (L[0], load[0], and_3_out);
  assign out_6 = L | H | I;  // OR_Gate or_1, 8 bits wide
  and and_12 (H[7], and_2_out, hold[7]);
  and and_13 (H[6], and_2_out, hold[6]);
  and and_14 (H[5], and_2_out, hold[5]);
  and and_15 (H[4], and_2_out, hold[4]);
  and and_16 (H[3], hold[3], and_2_out);
  and and_17 (H[2], hold[2], and_2_out);
  and and_18 (H[1], hold[1], and_2_out);
  and and_19 (H[0], hold[0], and_2_out);
  and and_20 (I[7], and_1_out, increment[7]);
  and and_21 (I[6], and_1_out, increment[6]);
  and and_22 (I[5], and_1_out, increment[5]);
  and and_23 (I[4], and_1_out, increment[4]);
  and and_24 (I[3], increment[3], and_1_out);
  and and_25 (I[2], increment[2], and_1_out);
  and and_26 (I[1], increment[1], and_1_out);
  and and_27 (I[0], increment[0], and_1_out);
endmodule

module full_adder (
  input  A,
  input  B,
  input  Cin,
  output Cout,
  output S
);

  wire and_1_out, and_2_out, and_3_out, xor_1_out;

  and and_1 (and_1_out, A, B);
  and and_2 (and_2_out, Cin, B);
  and and_3 (and_3_out, A, Cin);
  xor xor_1 (xor_1_out, A, B);
  or or_1 (Cout, and_1_out, and_2_out, and_3_out);
  xor xor_2 (S, xor_1_out, Cin);
endmodule

module priority_control (
  input  reset,
  input  load,
  input  hold,
  input  enable,
  output out_5,
  output out_6
);

  wire and_1_out, and_2_out, and_3_out, not_1_out, not_2_out, not_3_out;

  not not_1 (not_1_out, reset);
  not not_2 (not_2_out, load);
  not not_3 (not_3_out, hold);
  and and_1 (and_1_out, not_1_out, load);
  and and_2 (and_2_out, not_1_out, not_2_out, hold);
  and and_3 (and_3_out, not_2_out, not_1_out, not_3_out, enable);
  or or_1 (out_5, and_2_out, and_3_out);
  or or_2 (out_6, and_1_out, and_3_out);
endmodule

module display (
  input  [7:0] in_1,
  output [3:0] out_2,
  output [3:0] out_3,
  output [3:0] out_4
);

  wire [7:0] divider_1_out, divider_2_out;
  wire [7:4] divider_1_rem, divider_2_rem, divider_3_rem;

  Divider divider_1 (.a(in_1), .b(8'ha), .out(divider_1_out), .upper({8{1'b0}}), .rem({divider_1_rem, out_4}));
  Divider divider_2 (.a(divider_1_out), .b(8'ha), .out(divider_2_out), .upper({8{1'b0}}), .rem({divider_2_rem, out_3}));
  Divider divider_3 (.a(divider_2_out), .b(8'ha), .upper({8{1'b0}}), .rem({divider_3_rem, out_2}));  // open: out
endmodule
