// Logisim project fsm_controller.circ as structural Verilog: 4 circuits, main circuit main
module main (
  input  rest,
  input  X
);

  wire clock_1_out, next_state_logic_1_n0, next_state_logic_1_n1, output_logic_1_out_3, output_logic_1_out_4,
       output_logic_1_out_5, output_logic_1_out_6, state_register_1_q0, state_register_1_q1;

  Clock clock_1 (.out(clock_1_out));
  LED led_1 (.in(output_logic_1_out_3));
  LED led_2 (.in(output_logic_1_out_4));
  LED led_3 (.in(output_logic_1_out_5));
  LED led_4 (.in(output_logic_1_out_6));
  state_register state_register_1 (
    .CLK(clock_1_out), .R(rest), .I1(next_state_logic_1_n1), .I0(next_state_logic_1_n0),
    .Q1(state_register_1_q1), .Q0(state_register_1_q0));
  next_state_logic next_state_logic_1 (
    .X(X), .Q1(state_register_1_q1), .Q0(state_register_1_q0), .N1(next_state_logic_1_n1),
    .N0(next_state_logic_1_n0));
  output_logic output_logic_1 (
    .Q1(state_register_1_q1), .Q0(state_register_1_q0), .out_3(output_logic_1_out_3),
    .out_4(output_logic_1_out_4), .out_5(output_logic_1_out_5), .out_6(output_logic_1_out_6));

  // Notes on the sheet:
  //   IDLE
  //   READ
  //   DONE
  //   PROCESS
endmodule

module state_register (
  input  CLK,
  input  R,
  input  I1,
  input  I0,
  output Q1,
  output Q0
);

  D_Flip_Flop d_ff_1 (.D(I1), .clk(CLK), .Q(Q1), .reset(R));  // open: Qn, preset
  D_Flip_Flop d_ff_2 (.D(I0), .clk(CLK), .Q(Q0), .reset(R));  // open: Qn, preset
endmodule

module next_state_logic (
  input  X,
  input  Q1,
  input  Q0,
  output N1,
  output N0
);

  wire and_1_out, and_3_out, and_4_out, not_1_out, not_2_out, not_3_out, xor_1_out;

  xor xor_1 (xor_1_out, Q1, Q0);
  not not_1 (not_1_out, Q1);
  and and_1 (and_1_out, not_1_out, Q0);
  not not_2 (not_2_out, and_1_out);
  not not_3 (not_3_out, X);
  and and_2 (N1, X, xor_1_out);
  and and_3 (and_3_out, X, not_2_out);
  and and_4 (and_4_out, not_3_out, and_1_out);
  or or_1 (N0, and_3_out, and_4_out);
endmodule

module output_logic (
  input  Q1,
  input  Q0,
  output out_3,
  output out_4,
  output out_5,
  output out_6
);

  wire not_1_out, not_2_out;

  not not_1 (not_1_out, Q1);
  not not_2 (not_2_out, Q0);
  and and_1 (out_3, not_1_out, not_2_out);
  and and_2 (out_4, not_1_out, Q0);
  and and_3 (out_5, Q1, not_2_out);
  and and_4 (out_6, Q1, Q0);
endmodule
